# Fritzing sketch piezo (saved by Fritzing 0.9.3b)
breadboards: 1

parts:
  부품2 = Arduino Uno (Rev3)
  HC-SR04_Sensor_1 = HC-SR04 Ultrasonic Distance Sensor

nets:
  N1: 부품2.D8, HC-SR04_Sensor_1.ECHO
  N2: 부품2.D7, HC-SR04_Sensor_1.TRIG
  5V: 부품2.5V, HC-SR04_Sensor_1.VCC
  GND: 부품2.GND, HC-SR04_Sensor_1.GND
