# Fritzing sketch 조도센서 (saved by Fritzing 0.9.3b)
breadboards: 1

parts:
  부품2 = Arduino Uno (Rev3)
  R1 = Resistor [tolerance=±5% resistance=10k package=THT]
  R2 = Photocell (LDR) [package=THT]
  R3 = Resistor [tolerance=±5% resistance=220 package=THT]
  LED1 = LED - 5mm [color="Red (633nm)" package="5 mm [THT]"]

nets:
  N1: 부품2.A0, R1.Pin_1, R2.pin_0
  N2: 부품2.D3_PWM, LED1.anode
  N3: 부품2.5V, R2.pin_1
  N4: 부품2.GND, R1.Pin_0, R3.Pin_0
  N5: R3.Pin_1, LED1.cathode
